// Logisim project Sesion8_Display7Seg_Latches.circ as structural Verilog: 4 circuits, main circuit main
module Decodificador_7Seg (
  input  X3,
  input  X2,
  input  X1,
  input  X0,
  output a,
  output b,
  output c,
  output d,
  output e,
  output f,
  output g
);

  wire nX0, nX1, nX2, nX3, t1, t2, t3, t4, t5, t6, t7, t8, t9, t10, t11, t12, t13, t14, t15, t16, t17, t18,
       t19, t20, t21, t22, t23, t24, t25, t26, t27, t28, t29, t30, t31, t32, t33, t34, t35, t36, t37, t38,
       t39, t40, t41, t42, t43, t44, t45, t46, t47, t48, t49, t50, t51;

  // NOT_Gate not_1: pin names not known; wires that end beside it: X3, nX3
  and and_1 (t1, nX2, nX0);
  and and_2 (t5, nX3, X2);
  or or_1 (t9, t1, t2);
  or or_2 (a, t12, t8);
  and and_3 (t16, t4, X0);
  or or_3 (t20, t19, t15);
  and and_4 (t23, nX2, X0);
  or or_4 (c, t26, t7);
  and and_5 (t30, t29, X0);
  or or_5 (t34, t28, t30);
  and and_6 (t37, X1, nX0);
  or or_6 (t41, t40, t38);
  and and_7 (t44, t5, nX1);
  or or_7 (f, t47, t44);
  or or_8 (t51, t50, t7);
  // NOT_Gate not_2: pin names not known; wires that end beside it: X2, nX2
  and and_8 (t2, X2, X1);
  and and_9 (t6, t5, X0);
  or or_9 (t10, t9, t3);
  and and_10 (t13, nX2, nX1);
  and and_11 (t17, X3, nX1);
  or or_10 (t21, t20, t16);
  or or_11 (t24, t22, t23);
  and and_12 (t27, nX2, X1);
  and and_13 (t31, t2, nX0);
  or or_12 (t35, t34, t31);
  and and_14 (t38, X3, X1);
  or or_13 (e, t41, t39);
  or or_14 (t45, t42, t43);
  and and_15 (t48, X3, X0);
  or or_15 (g, t51, t44);
  // NOT_Gate not_3: pin names not known; wires that end beside it: X1, nX1
  and and_16 (t3, X3, nX0);
  and and_17 (t7, X3, nX2);
  or or_16 (t11, t10, t4);
  and and_18 (t14, nX3, nX1);
  and and_19 (t18, t17, X0);
  or or_17 (b, t21, t18);
  or or_18 (t25, t24, t13);
  and and_20 (t28, t27, X0);
  and and_21 (t32, nX3, nX2);
  or or_19 (t36, t35, t17);
  and and_22 (t39, X3, X2);
  and and_23 (t42, nX1, nX0);
  or or_20 (t46, t45, t38);
  or or_21 (t49, t37, t27);
  // NOT_Gate not_4: pin names not known; wires that end beside it: X0, nX0
  and and_24 (t4, nX3, X1);
  and and_25 (t8, t7, nX1);
  or or_22 (t12, t11, t6);
  and and_26 (t15, t14, nX0);
  or or_23 (t19, t1, t13);
  and and_27 (t22, nX1, X0);
  or or_24 (t26, t25, t5);
  and and_28 (t29, X2, nX1);
  and and_29 (t33, t32, nX0);
  or or_25 (d, t36, t33);
  or or_26 (t40, t37, t1);
  and and_30 (t43, X2, nX0);
  or or_27 (t47, t46, t7);
  or or_28 (t50, t49, t48);

  // Notes on the sheet:
  //   Decodificador hexadecimal a 7 segmentos (0-9, A, b, C, d, E, F) - compuertas de 2 entradas
endmodule

module Latch_SR (
  input  S,
  input  R,
  output Q,
  output Qn
);

  nor nor_1 (Qn, S, Q);
  nor nor_2 (Q, Qn, R);

  // Notes on the sheet:
  //   Latch S-R (NOR): S=1,R=0 -> Q=1 | S=0,R=1 -> Q=0 | S=R=0 -> mantiene | S=R=1 -> inválido
endmodule

module Latch_D (
  input  D,
  input  EN,
  output Q,
  output Qn
);

  wire nD, R, S;

  // NOT_Gate not_1: pin names not known; wires that end beside it: D, nD
  and and_1 (S, D, EN);
  and and_2 (R, nD, EN);
  nor nor_1 (Qn, S, Q);
  nor nor_2 (Q, Qn, R);

  // Notes on the sheet:
  //   Latch D con habilitación: EN=1 -> Q=D | EN=0 -> mantiene
endmodule

module main (
  input  X3,
  input  X2,
  input  X1,
  input  X0,
  input  S,
  input  R,
  input  D,
  input  EN
);

  wire a, b, c, d_t, e, f, g, latch_d_1_q, latch_d_1_qn, latch_sr_1_q, latch_sr_1_qn;

  Decodificador_7Seg decodificador_7seg_1 (
    .X3(X3), .X2(X2), .X1(X1), .X0(X0), .a(a), .b(b), .c(c), .d(d_t), .e(e), .f(f), .g(g));
  Latch_SR latch_sr_1 (.S(S), .R(R), .Q(latch_sr_1_q), .Qn(latch_sr_1_qn));
  Latch_D latch_d_1 (.D(D), .EN(EN), .Q(latch_d_1_q), .Qn(latch_d_1_qn));
  LED Q (.in(latch_sr_1_q));
  LED Q_prime (.in(latch_sr_1_qn));
  LED Q_2 (.in(latch_d_1_q));
  LED Q_prime_2 (.in(latch_d_1_qn));
  _7_Segment_Display u_7_segment_display_1 (.g(g), .f(f), .a(a), .b(b), .e(e), .d(d_t), .c(c), .dp(1'b0));

  // Notes on the sheet:
  //   UNIVERSIDAD NACIONAL "SAN LUIS GONZAGA" - FACULTAD DE INGENIERÍA DE SISTEMAS
  //   Curso: Fundamentos de Electrónica Digital - Docente: Mag. Freddy Gustavo Ventura Fernandez
  //   Sesión 8: Display de 7 segmentos (hexadecimal) y Latches S-R / D
  //   INTEGRANTES:
  //   1. Vivar Farfán, Miguel Alonso
  //   2. Estudiante 2: ____________________
  //   3. Estudiante 3: ____________________
  //   4. Estudiante 4: ____________________
  //   1) Display de 7 segmentos: X3 (MSB) ... X0 (LSB). 0-9 y A, b, C, d, E, F
  //   2) Latch S-R (circuito Latch_SR). Primero aplicar SET o RESET (S=R=0 inicial es indefinido).
  //   3) Latch D con habilitación (circuito Latch_D)
  //   Salidas a-g activas en alto
endmodule
